# Fritzing sketch breadboard (saved by Fritzing 0.9.3b)
breadboards: 1

parts:
  Part1 = Arduino Micro (Rev3)  # not connected
  Part2 = Breakout Board for Electret Microphone  # not connected
  S1 = Pushbutton [package="[THT]"]
  MIC1 = Microphone

nets:
  N1: S1.Pin_1, S1.Pin_2, MIC1.pin1
  N2: S1.Pin_3, S1.Pin_4
